# Fritzing sketch silentglade (saved by Fritzing 0.9.2b)
perfboards: 1

parts:
  R1 = Rotary Potentiometer (Small) [maximum_resistance=1kΩ package=THT]
  R2 = Photocell (LDR) [package=THT]
  Q1 = MOSFET-NCHANNEL [package=to-92]
  R3 = Photocell (LDR) [package=THT]
  R4 = Photocell (LDR) [package=THT]

nets (from the schematic view):
  N1: R1.wiper, R2.pin_1, Q1.G, R3.pin_1, R4.pin_1
  5V: R1.leg2
  GND: R2.pin_0, Q1.S, R3.pin_0, R4.pin_0
  to button: Q1.D
